// Logisim project lab06part2.circ as structural Verilog: 1 circuit, main circuit main
module main (
  input  in_1,
  input  [7:0] in_2,
  input  [7:0] in_3,
  input  in_4,
  output [7:0] out_5,
  output [7:0] out_6,
  output [7:0] out_7
);

  Adder adder_1 (.a(in_2), .b(in_3), .out(out_5), .cin(in_1));  // open: cout
  Subtractor subtractor_1 (.a(in_2), .b(in_3), .out(out_7), .bin(in_1));  // open: bout
  Multiplexer #(.width(8), .enable("false")) multiplexer_1 (.in0(out_5), .in1(out_7), .out(out_6), .sel(in_4));

  // Notes on the sheet:
  //   out_5: pull=up
  //   out_6: pull=up
endmodule
