// Logisim project lab08.circ as structural Verilog: 3 circuits, main circuit main
module main (
  input  [7:0] A,
  input  Ainv,
  input  Binv,
  input  [1:0] in_4,
  input  [7:0] B,
  output Zero,
  output [7:0] Result,
  output Overflow
);

  wire and_1_out, and_2_out, bit7alu_1_ao, bit7alu_1_bo, bit7alu_1_set, bitalu_1_carryout, bitalu_2_carryout,
       bitalu_3_carryout, bitalu_4_carryout, bitalu_5_carryout, bitalu_6_carryout, bitalu_7_carryout,
       not_1_out, not_2_out, not_3_out, xor_1_out;

  not not_1 (not_1_out, bit7alu_1_bo);
  not not_2 (not_2_out, bit7alu_1_ao);
  bitALU bitalu_1 (
    .A(A[0]), .B(B[0]), .Less(xor_1_out), .Ainv(Ainv), .Binv(Binv), .CarryIn(Binv), .OP(in_4),
    .CarryOut(bitalu_1_carryout), .Result(Result[0]));  // open: Set
  bitALU bitalu_2 (
    .A(A[1]), .B(B[1]), .Less(1'b0), .Ainv(Ainv), .Binv(Binv), .CarryIn(bitalu_1_carryout), .OP(in_4),
    .CarryOut(bitalu_2_carryout), .Result(Result[1]));  // open: Set
  bitALU bitalu_3 (
    .A(A[2]), .B(B[2]), .Less(1'b0), .Ainv(Ainv), .Binv(Binv), .CarryIn(bitalu_2_carryout), .OP(in_4),
    .CarryOut(bitalu_3_carryout), .Result(Result[2]));  // open: Set
  bitALU bitalu_4 (
    .A(A[3]), .B(B[3]), .Less(1'b0), .Ainv(Ainv), .Binv(Binv), .CarryIn(bitalu_3_carryout), .OP(in_4),
    .CarryOut(bitalu_4_carryout), .Result(Result[3]));  // open: Set
  bitALU bitalu_5 (
    .A(A[4]), .B(B[4]), .Less(1'b0), .Ainv(Ainv), .Binv(Binv), .CarryIn(bitalu_4_carryout), .OP(in_4),
    .CarryOut(bitalu_5_carryout), .Result(Result[4]));  // open: Set
  bitALU bitalu_6 (
    .A(A[5]), .B(B[5]), .Less(1'b0), .Ainv(Ainv), .Binv(Binv), .CarryIn(bitalu_5_carryout), .OP(in_4),
    .CarryOut(bitalu_6_carryout), .Result(Result[5]));  // open: Set
  bitALU bitalu_7 (
    .A(A[6]), .B(B[6]), .Less(1'b0), .Ainv(Ainv), .Binv(Binv), .CarryIn(bitalu_6_carryout), .OP(in_4),
    .CarryOut(bitalu_7_carryout), .Result(Result[6]));  // open: Set
  bit7ALU bit7alu_1 (
    .A(A[7]), .B(B[7]), .Less(1'b0), .Ainv(Ainv), .Binv(Binv), .CarryIn(bitalu_7_carryout), .OP(in_4),
    .Ao(bit7alu_1_ao), .Bo(bit7alu_1_bo), .Set(bit7alu_1_set), .Result(Result[7]));  // open: CarryOut
  not not_3 (not_3_out, bit7alu_1_set);
  and and_1 (and_1_out, not_1_out, not_2_out, bit7alu_1_set);
  and and_2 (and_2_out, bit7alu_1_bo, bit7alu_1_ao, not_3_out);
  or or_1 (Overflow, and_1_out, and_2_out);
  xor xor_1 (xor_1_out, bit7alu_1_set, Overflow);
  nor nor_1 (Zero, Result[0], Result[1], Result[2], Result[3], Result[4], Result[5], Result[6], Result[7]);
endmodule

module bitALU (
  input  Ainv,
  input  Binv,
  input  CarryIn,
  input  [1:0] OP,
  input  A,
  input  B,
  input  Less,
  output Result,
  output CarryOut,
  output Set
);

  wire and_1_out, multiplexer_1_out, multiplexer_2_out, not_1_out, not_2_out, or_1_out;

  Multiplexer multiplexer_1 (.in0(A), .in1(not_1_out), .out(multiplexer_1_out), .sel(Ainv));  // open: en
  not not_1 (not_1_out, A);
  Multiplexer multiplexer_2 (.in0(B), .in1(not_2_out), .out(multiplexer_2_out), .sel(Binv));  // open: en
  not not_2 (not_2_out, B);
  and and_1 (and_1_out, multiplexer_1_out, multiplexer_2_out);
  or or_1 (or_1_out, multiplexer_1_out, multiplexer_2_out);
  Adder #(.width(1)) adder_1 (.a(multiplexer_1_out), .b(multiplexer_2_out), .out(Set), .cin(CarryIn), .cout(CarryOut));
  Multiplexer #(.select(2)) multiplexer_3 (
    .in0(and_1_out), .in1(or_1_out), .in2(Set), .in3(Less), .out(Result), .sel(OP));  // open: en
endmodule

module bit7ALU (
  input  Ainv,
  input  Binv,
  input  CarryIn,
  input  [1:0] OP,
  input  A,
  input  B,
  input  Less,
  output Result,
  output Ao,
  output Bo,
  output CarryOut,
  output Set
);

  wire and_1_out, not_1_out, not_2_out, or_1_out;

  Multiplexer multiplexer_1 (.in0(A), .in1(not_1_out), .out(Ao), .sel(Ainv));  // open: en
  not not_1 (not_1_out, A);
  Multiplexer multiplexer_2 (.in0(B), .in1(not_2_out), .out(Bo), .sel(Binv));  // open: en
  not not_2 (not_2_out, B);
  and and_1 (and_1_out, Ao, Bo);
  or or_1 (or_1_out, Ao, Bo);
  Adder #(.width(1)) adder_1 (.a(Ao), .b(Bo), .out(Set), .cin(CarryIn), .cout(CarryOut));
  Multiplexer #(.select(2)) multiplexer_3 (
    .in0(and_1_out), .in1(or_1_out), .in2(Set), .in3(Less), .out(Result), .sel(OP));  // open: en
endmodule
