// Logisim project lab09.circ as structural Verilog
module RegisterFile (
  input  writeEnable,
  input  [2:0] ReadRegister1,
  input  [2:0] ReadRegister2,
  input  [2:0] WriteRegister,
  input  [31:0] WriteData,
  input  Clock,
  output [31:0] ReadData1,
  output [31:0] ReadData2
);

  wire and_1_out, and_2_out, and_3_out, and_4_out, and_5_out, and_6_out, and_7_out, and_8_out,
       decoder_1_out0, decoder_1_out1, decoder_1_out2, decoder_1_out3, decoder_1_out4, decoder_1_out5,
       decoder_1_out6, decoder_1_out7;
  wire [31:0] register_1_q, register_2_q, register_3_q, register_4_q, register_5_q, register_6_q,
       register_7_q, register_8_q;

  Decoder #(.select(3)) decoder_1 (
    .out0(decoder_1_out0), .out1(decoder_1_out1), .out2(decoder_1_out2), .out3(decoder_1_out3),
    .out4(decoder_1_out4), .out5(decoder_1_out5), .out6(decoder_1_out6), .out7(decoder_1_out7),
    .sel(WriteRegister));  // open: en
  Register #(.width(32)) register_1 (.D(WriteData), .en(and_1_out), .Q(register_1_q), .clk(Clock));  // open: clr
  and and_1 (and_1_out, decoder_1_out0, writeEnable);
  Register #(.width(32)) register_2 (.D(WriteData), .en(and_2_out), .Q(register_2_q), .clk(Clock));  // open: clr
  and and_2 (and_2_out, decoder_1_out1, writeEnable);
  Register #(.width(32)) register_3 (.D(WriteData), .en(and_3_out), .Q(register_3_q), .clk(Clock));  // open: clr
  and and_3 (and_3_out, decoder_1_out2, writeEnable);
  Register #(.width(32)) register_4 (.D(WriteData), .en(and_4_out), .Q(register_4_q), .clk(Clock));  // open: clr
  and and_4 (and_4_out, decoder_1_out3, writeEnable);
  Register #(.width(32)) register_5 (.D(WriteData), .en(and_5_out), .Q(register_5_q), .clk(Clock));  // open: clr
  and and_5 (and_5_out, decoder_1_out4, writeEnable);
  Register #(.width(32)) register_6 (.D(WriteData), .en(and_6_out), .Q(register_6_q), .clk(Clock));  // open: clr
  and and_6 (and_6_out, decoder_1_out5, writeEnable);
  Register #(.width(32)) register_7 (.D(WriteData), .en(and_7_out), .Q(register_7_q), .clk(Clock));  // open: clr
  and and_7 (and_7_out, decoder_1_out6, writeEnable);
  Register #(.width(32)) register_8 (.D(WriteData), .en(and_8_out), .Q(register_8_q), .clk(Clock));  // open: clr
  and and_8 (and_8_out, decoder_1_out7, writeEnable);
  Multiplexer #(.select(3), .width(32)) multiplexer_1 (
    .in0(register_1_q), .in1(register_2_q), .in2(register_3_q), .in3(register_4_q), .in4(register_5_q),
    .in5(register_6_q), .in6(register_7_q), .in7(register_8_q), .out(ReadData1), .sel(ReadRegister1));  // open: en
  Multiplexer #(.select(3), .width(32)) multiplexer_2 (
    .in0(register_1_q), .in1(register_2_q), .in2(register_3_q), .in3(register_4_q), .in4(register_5_q),
    .in5(register_6_q), .in6(register_7_q), .in7(register_8_q), .out(ReadData2), .sel(ReadRegister2));  // open: en
endmodule
