// Logisim project lab10.circ as structural Verilog: 4 circuits, main circuit main
module main (
);

  wire clock_1_out, decoder_1_mux, fields_1_ra, not_1_out;
  wire [1:0] decoder_1_alu;
  wire [3:0] fields_1_opcode;
  wire [7:0] adder_1_out, alu_1_data, B_2_q, B_q, fields_1_immediate, multiplexer_1_out, PC_q;
  wire [15:0] rom_1_data;

  Register PC (.D(adder_1_out), .en(1'b1), .Q(PC_q), .clk(clock_1_out));  // open: clr
  Clock clock_1 (.out(clock_1_out));
  Adder adder_1 (.a(8'h1), .b(PC_q), .out(adder_1_out), .cin(1'b0));  // open: cout
  ROM #(.dataWidth(16)) rom_1 (.addr(PC_q), .data(rom_1_data), .sel(1'b1));
  not not_1 (not_1_out, fields_1_ra);
  Fields fields_1 (.Input(rom_1_data), .Opcode(fields_1_opcode), .ra(fields_1_ra), .Immediate(fields_1_immediate));
  Decoder decoder_1 (.Opcode(fields_1_opcode), .ALU(decoder_1_alu), .Mux(decoder_1_mux));
  Register B (.D(multiplexer_1_out), .en(not_1_out), .Q(B_q), .clk(clock_1_out));  // open: clr
  Register B_2 (.D(multiplexer_1_out), .en(fields_1_ra), .Q(B_2_q), .clk(clock_1_out));  // open: clr
  ALU alu_1 (.A(B_q), .B(B_2_q), .Operation(decoder_1_alu), .Data(alu_1_data));
  Multiplexer #(.width(8), .enable("false")) multiplexer_1 (
    .in0(alu_1_data), .in1(fields_1_immediate), .out(multiplexer_1_out), .sel(decoder_1_mux));

  // Notes on the sheet:
  //   contents of rom_1 (hex, n*v repeats v):
  //   1 802
endmodule

module ALU (
  input  [7:0] A,
  input  [7:0] B,
  output [1:0] Operation,
  output [7:0] Data
);

  wire [7:0] adder_1_out, and_1_out, or_1_out, subtractor_1_out;

  Adder adder_1 (.a(A), .b(B), .out(adder_1_out));  // open: cin, cout
  Subtractor subtractor_1 (.a(A), .b(B), .out(subtractor_1_out));  // open: bin, bout
  assign and_1_out = A & B;  // AND_Gate and_1, 8 bits wide
  assign or_1_out = A | B;  // OR_Gate or_1, 8 bits wide
  Multiplexer #(.select(2), .width(8)) multiplexer_1 (
    .in0(adder_1_out), .in1(subtractor_1_out), .in2(or_1_out), .in3(and_1_out), .out(Data), .sel(Operation));  // open: en
endmodule

module Fields (
  input  [15:0] Input,
  output [3:0] Opcode,
  output ra,
  output [7:0] Immediate
);


  assign Immediate = Input[7:0];
  assign Opcode = Input[15:12];
  assign ra = Input[11];
endmodule

module Decoder (
  input  [3:0] Opcode,
  output [1:0] ALU,
  output Mux
);

  wire not_2_out;

  not not_1 (ALU[1], Opcode[1]);
  not not_2 (not_2_out, Opcode[2]);
  and and_1 (Mux, ALU[1], not_2_out);

  assign ALU[0] = Opcode[0];
endmodule
