// Logisim project calculatorCPU.circ as structural Verilog: 18 circuits, main circuit main
module main (
);

  wire _0_out, _1_out, _2_out, _3_out, _4_out, _5_out, _6_out, _7_out, _8_out, _9_out, ALU_zero, and_1_out,
       and_2_out, button_2_out, button_3_out, button_4_out, button_5_out, button_out, C_out, clock_1_out,
       control_unit_to_do_1_alusrc, control_unit_to_do_1_beq, control_unit_to_do_1_bne,
       control_unit_to_do_1_jump, control_unit_to_do_1_regdst, control_unit_to_do_1_regwrite,
       keypad_controller_1_write, not_1_out, or_1_out;
  wire [2:0] lcd_controller_1__7_segment_3_2, lcd_controller_1__7_segment_5_2,
       lcd_controller_1__7_segment_7_2, lcd_controller_1__7_segment_9_2, lcd_controller_1_minus_2;
  wire [3:0] control_unit_to_do_1_aluop, lcd_controller_1__7_segment_3, lcd_controller_1__7_segment_5,
       lcd_controller_1__7_segment_7, lcd_controller_1__7_segment_9, lcd_controller_1_minus;
  wire [4:0] multiplexer_1_out;
  wire [5:0] ALUcontrol_controloutput;
  wire [6:0] lcd_controller_1__7_segment_0, lcd_controller_1__7_segment_1, lcd_controller_1__7_segment_2,
       lcd_controller_1__7_segment_4, lcd_controller_1__7_segment_6, lcd_controller_1__7_segment_8;
  wire [15:0] PC_pcoutput_prime;
  wire [27:0] SL2_jumpaddress;
  wire [31:0] adder_1_out, ALU_result, keypad_controller_1_output, multiplexer_2_out, multiplexer_3_out,
       multiplexer_4_out, PCadd4_output, RegFile_readdata1, RegFile_readdata2, RegFile_t8_to_lcd,
       RegFile_t9_to_keypad, ROM_dataoutput, shift_left_to_do_1_output, SignExtend_out_2;

  Clock clock_1 (.out(clock_1_out));
  PCadd4 PCadd4 (.PCinput(PC_pcoutput_prime), .Output(PCadd4_output));
  PC PC (.PCInput(multiplexer_4_out), .Clock(clock_1_out), .PCoutput_prime(PC_pcoutput_prime));
  Instruction_Memory__TO_DO ROM (.PC(PC_pcoutput_prime), .DataOutput(ROM_dataoutput));
  ShiftLeft2 SL2 (.Input(ROM_dataoutput[25:0]), .JumpAddress(SL2_jumpaddress));
  Sign_Extend__TO_DO SignExtend (.Input(ROM_dataoutput[15:0]), .out_2(SignExtend_out_2));
  Control_Unit__TO_DO control_unit_to_do_1 (
    .OPcode(ROM_dataoutput[31:26]), .RegDST(control_unit_to_do_1_regdst), .Jump(control_unit_to_do_1_jump),
    .bne(control_unit_to_do_1_bne), .beq(control_unit_to_do_1_beq), .ALUop(control_unit_to_do_1_aluop),
    .ALUsrc(control_unit_to_do_1_alusrc), .RegWrite(control_unit_to_do_1_regwrite));
  Multiplexer #(.width(5), .enable("false")) multiplexer_1 (
    .in0(ROM_dataoutput[20:16]), .in1(ROM_dataoutput[15:11]), .out(multiplexer_1_out),
    .sel(control_unit_to_do_1_regdst));
  Shift_Left__TO_DO shift_left_to_do_1 (.Input(SignExtend_out_2), .Shamt(5'b00010), .Output(shift_left_to_do_1_output));
  Register_File__TO_DO RegFile (
    .ReadReg1(ROM_dataoutput[25:21]), .ReadReg2(ROM_dataoutput[20:16]), .WriteRegister(multiplexer_1_out),
    .WriteData(ALU_result), .Write_t9Keypad(keypad_controller_1_output),
    .WriteSignalKeypad(keypad_controller_1_write), .RegWrite(control_unit_to_do_1_regwrite),
    .Clock(clock_1_out), .ReadData1(RegFile_readdata1), .ReadData2(RegFile_readdata2),
    .t8_to_LCD(RegFile_t8_to_lcd), .t9_to_Keypad(RegFile_t9_to_keypad));
  Adder #(.width(32)) adder_1 (.a(PCadd4_output), .b(shift_left_to_do_1_output), .out(adder_1_out));  // open: cin, cout
  and and_1 (and_1_out, control_unit_to_do_1_beq, ALU_zero);
  Multiplexer #(.width(32), .enable("false")) multiplexer_2 (
    .in0(RegFile_readdata2), .in1(SignExtend_out_2), .out(multiplexer_2_out),
    .sel(control_unit_to_do_1_alusrc));
  ALUcontrol ALUcontrol (
    .funct(ROM_dataoutput[5:0]), .OP(control_unit_to_do_1_aluop), .ControlOutput(ALUcontrol_controloutput));
  Multiplexer #(.width(32), .enable("false")) multiplexer_3 (
    .in0(PCadd4_output), .in1(adder_1_out), .out(multiplexer_3_out), .sel(or_1_out));
  or or_1 (or_1_out, and_1_out, and_2_out);
  and and_2 (and_2_out, control_unit_to_do_1_bne, not_1_out);
  not not_1 (not_1_out, ALU_zero);
  _32_bit_ALU__TO_DO ALU (
    .A(RegFile_readdata1), .B(multiplexer_2_out), .Shamt(ROM_dataoutput[10:6]),
    .Control(ALUcontrol_controloutput), .Zero(ALU_zero), .Result(ALU_result));
  Multiplexer #(.width(32), .enable("false")) multiplexer_4 (
    .in0(multiplexer_3_out), .in1({PCadd4_output[31:28], SL2_jumpaddress}), .out(multiplexer_4_out),
    .sel(control_unit_to_do_1_jump));
  Keypad_Controller keypad_controller_1 (
    .C(C_out), .in_2(button_out), .in_3(button_5_out), .in_4(button_4_out), .in_5(button_3_out),
    .in_6(button_2_out), ._9(_9_out), ._8(_8_out), ._7(_7_out), ._6(_6_out), ._5(_5_out), ._4(_4_out),
    ._3(_3_out), ._2(_2_out), ._1(_1_out), ._0(_0_out), .From__t9(RegFile_t9_to_keypad),
    .Write(keypad_controller_1_write), .Output(keypad_controller_1_output));
  _7_Segment_Display u_7_segment_display_1 (
    .g(lcd_controller_1__7_segment_9[0]), .f(lcd_controller_1__7_segment_9[1]),
    .a(lcd_controller_1__7_segment_9[2]), .b(lcd_controller_1__7_segment_9[3]),
    .e(lcd_controller_1__7_segment_9_2[0]), .d(lcd_controller_1__7_segment_9_2[1]),
    .c(lcd_controller_1__7_segment_9_2[2]));  // open: dp
  _7_Segment_Display u_7_segment_display_2 (
    .g(lcd_controller_1_minus[0]), .f(lcd_controller_1_minus[1]), .a(lcd_controller_1_minus[2]),
    .b(lcd_controller_1_minus[3]), .e(lcd_controller_1_minus_2[0]), .d(lcd_controller_1_minus_2[1]),
    .c(lcd_controller_1_minus_2[2]));  // open: dp
  LCD_Controller lcd_controller_1 (
    .From__t8(RegFile_t8_to_lcd), .Minus({lcd_controller_1_minus_2, lcd_controller_1_minus}),
    ._7_Segment_9({lcd_controller_1__7_segment_9_2, lcd_controller_1__7_segment_9}),
    ._7_Segment_8(lcd_controller_1__7_segment_8),
    ._7_Segment_7({lcd_controller_1__7_segment_7_2, lcd_controller_1__7_segment_7}),
    ._7_Segment_6(lcd_controller_1__7_segment_6),
    ._7_Segment_5({lcd_controller_1__7_segment_5_2, lcd_controller_1__7_segment_5}),
    ._7_Segment_4(lcd_controller_1__7_segment_4),
    ._7_Segment_3({lcd_controller_1__7_segment_3_2, lcd_controller_1__7_segment_3}),
    ._7_Segment_2(lcd_controller_1__7_segment_2), ._7_Segment_1(lcd_controller_1__7_segment_1),
    ._7_Segment_0(lcd_controller_1__7_segment_0));
  _7_Segment_Display u_7_segment_display_3 (
    .g(lcd_controller_1__7_segment_8[0]), .f(lcd_controller_1__7_segment_8[1]),
    .a(lcd_controller_1__7_segment_8[2]), .b(lcd_controller_1__7_segment_8[3]),
    .e(lcd_controller_1__7_segment_8[4]), .d(lcd_controller_1__7_segment_8[5]),
    .c(lcd_controller_1__7_segment_8[6]));  // open: dp
  _7_Segment_Display u_7_segment_display_4 (
    .g(lcd_controller_1__7_segment_7[0]), .f(lcd_controller_1__7_segment_7[1]),
    .a(lcd_controller_1__7_segment_7[2]), .b(lcd_controller_1__7_segment_7[3]),
    .e(lcd_controller_1__7_segment_7_2[0]), .d(lcd_controller_1__7_segment_7_2[1]),
    .c(lcd_controller_1__7_segment_7_2[2]));  // open: dp
  _7_Segment_Display u_7_segment_display_5 (
    .g(lcd_controller_1__7_segment_6[0]), .f(lcd_controller_1__7_segment_6[1]),
    .a(lcd_controller_1__7_segment_6[2]), .b(lcd_controller_1__7_segment_6[3]),
    .e(lcd_controller_1__7_segment_6[4]), .d(lcd_controller_1__7_segment_6[5]),
    .c(lcd_controller_1__7_segment_6[6]));  // open: dp
  _7_Segment_Display u_7_segment_display_6 (
    .g(lcd_controller_1__7_segment_5[0]), .f(lcd_controller_1__7_segment_5[1]),
    .a(lcd_controller_1__7_segment_5[2]), .b(lcd_controller_1__7_segment_5[3]),
    .e(lcd_controller_1__7_segment_5_2[0]), .d(lcd_controller_1__7_segment_5_2[1]),
    .c(lcd_controller_1__7_segment_5_2[2]));  // open: dp
  Button _7 (.out(_7_out));
  Button _4 (.out(_4_out));
  Button _1 (.out(_1_out));
  Button _0 (.out(_0_out));
  _7_Segment_Display u_7_segment_display_7 (
    .g(lcd_controller_1__7_segment_4[0]), .f(lcd_controller_1__7_segment_4[1]),
    .a(lcd_controller_1__7_segment_4[2]), .b(lcd_controller_1__7_segment_4[3]),
    .e(lcd_controller_1__7_segment_4[4]), .d(lcd_controller_1__7_segment_4[5]),
    .c(lcd_controller_1__7_segment_4[6]));  // open: dp
  _7_Segment_Display u_7_segment_display_8 (
    .g(lcd_controller_1__7_segment_3[0]), .f(lcd_controller_1__7_segment_3[1]),
    .a(lcd_controller_1__7_segment_3[2]), .b(lcd_controller_1__7_segment_3[3]),
    .e(lcd_controller_1__7_segment_3_2[0]), .d(lcd_controller_1__7_segment_3_2[1]),
    .c(lcd_controller_1__7_segment_3_2[2]));  // open: dp
  Button _8 (.out(_8_out));
  Button _5 (.out(_5_out));
  Button _2 (.out(_2_out));
  Button C (.out(C_out));
  _7_Segment_Display u_7_segment_display_9 (
    .g(lcd_controller_1__7_segment_1[0]), .f(lcd_controller_1__7_segment_1[1]),
    .a(lcd_controller_1__7_segment_1[2]), .b(lcd_controller_1__7_segment_1[3]),
    .e(lcd_controller_1__7_segment_1[4]), .d(lcd_controller_1__7_segment_1[5]),
    .c(lcd_controller_1__7_segment_1[6]));  // open: dp
  _7_Segment_Display u_7_segment_display_10 (
    .g(lcd_controller_1__7_segment_2[0]), .f(lcd_controller_1__7_segment_2[1]),
    .a(lcd_controller_1__7_segment_2[2]), .b(lcd_controller_1__7_segment_2[3]),
    .e(lcd_controller_1__7_segment_2[4]), .d(lcd_controller_1__7_segment_2[5]),
    .c(lcd_controller_1__7_segment_2[6]));  // open: dp
  Button _9 (.out(_9_out));
  Button _6 (.out(_6_out));
  Button _3 (.out(_3_out));
  Button button (.out(button_out));
  _7_Segment_Display u_7_segment_display_11 (
    .g(lcd_controller_1__7_segment_0[0]), .f(lcd_controller_1__7_segment_0[1]),
    .a(lcd_controller_1__7_segment_0[2]), .b(lcd_controller_1__7_segment_0[3]),
    .e(lcd_controller_1__7_segment_0[4]), .d(lcd_controller_1__7_segment_0[5]),
    .c(lcd_controller_1__7_segment_0[6]));  // open: dp
  Button button_2 (.out(button_2_out));
  Button button_3 (.out(button_3_out));
  Button button_4 (.out(button_4_out));
  Button button_5 (.out(button_5_out));

  // Notes on the sheet:
  //   Write Data to $t9
  //   Write Signal for $t9
  //   From $t8
  //   From $t9
endmodule

module LCD_Controller (
  input  [31:0] From__t8,
  output [6:0] Minus,
  output [6:0] _7_Segment_9,
  output [6:0] _7_Segment_8,
  output [6:0] _7_Segment_7,
  output [6:0] _7_Segment_6,
  output [6:0] _7_Segment_5,
  output [6:0] _7_Segment_4,
  output [6:0] _7_Segment_3,
  output [6:0] _7_Segment_2,
  output [6:0] _7_Segment_1,
  output [6:0] _7_Segment_0
);

  wire [3:0] binarytobcd_1_bcd0, binarytobcd_1_bcd1, binarytobcd_1_bcd2, binarytobcd_1_bcd3,
       binarytobcd_1_bcd4, binarytobcd_1_bcd5, binarytobcd_1_bcd6, binarytobcd_1_bcd7, binarytobcd_1_bcd8,
       binarytobcd_1_bcd9;

  BinaryToBCD binarytobcd_1 (
    .Input(From__t8), .Minus(Minus[0]), .BCD9(binarytobcd_1_bcd9), .BCD8(binarytobcd_1_bcd8),
    .BCD7(binarytobcd_1_bcd7), .BCD6(binarytobcd_1_bcd6), .BCD5(binarytobcd_1_bcd5),
    .BCD4(binarytobcd_1_bcd4), .BCD3(binarytobcd_1_bcd3), .BCD2(binarytobcd_1_bcd2),
    .BCD1(binarytobcd_1_bcd1), .BCD0(binarytobcd_1_bcd0));
  _7_Segment_Controller u_7_segment_controller_1 (.BCD(binarytobcd_1_bcd9), .out_2(_7_Segment_9));
  _7_Segment_Controller u_7_segment_controller_2 (.BCD(binarytobcd_1_bcd8), .out_2(_7_Segment_8));
  _7_Segment_Controller u_7_segment_controller_3 (.BCD(binarytobcd_1_bcd7), .out_2(_7_Segment_7));
  _7_Segment_Controller u_7_segment_controller_4 (.BCD(binarytobcd_1_bcd6), .out_2(_7_Segment_6));
  _7_Segment_Controller u_7_segment_controller_5 (.BCD(binarytobcd_1_bcd5), .out_2(_7_Segment_5));
  _7_Segment_Controller u_7_segment_controller_6 (.BCD(binarytobcd_1_bcd4), .out_2(_7_Segment_4));
  _7_Segment_Controller u_7_segment_controller_7 (.BCD(binarytobcd_1_bcd3), .out_2(_7_Segment_3));
  _7_Segment_Controller u_7_segment_controller_8 (.BCD(binarytobcd_1_bcd2), .out_2(_7_Segment_2));
  _7_Segment_Controller u_7_segment_controller_9 (.BCD(binarytobcd_1_bcd1), .out_2(_7_Segment_1));
  _7_Segment_Controller u_7_segment_controller_10 (.BCD(binarytobcd_1_bcd0), .out_2(_7_Segment_0));

  assign Minus[6:1] = {6{1'b0}};
endmodule

module _7_Segment_Controller (
  input  [3:0] BCD,
  output [6:0] out_2
);

  wire and_1_out, and_2_out, and_3_out, and_4_out, and_5_out, and_6_out, and_7_out, and_8_out, and_9_out,
       and_10_out, and_11_out, and_12_out, and_13_out, and_14_out, and_15_out, and_16_out, not_1_out,
       not_2_out, not_3_out, not_4_out, not_5_out, not_6_out, not_7_out, not_8_out, not_9_out, not_10_out,
       not_11_out, not_12_out, not_13_out, not_14_out, not_15_out, not_16_out, not_17_out, not_18_out,
       not_19_out, not_20_out, not_21_out;

  not not_1 (not_1_out, BCD[2]);
  not not_2 (not_2_out, BCD[0]);
  not not_3 (not_3_out, BCD[1]);
  not not_4 (not_4_out, BCD[1]);
  not not_5 (not_5_out, BCD[0]);
  not not_6 (not_6_out, BCD[1]);
  not not_7 (not_7_out, BCD[0]);
  not not_8 (not_8_out, BCD[2]);
  not not_9 (not_9_out, BCD[0]);
  not not_10 (not_10_out, BCD[1]);
  not not_11 (not_11_out, BCD[0]);
  not not_12 (not_12_out, BCD[2]);
  not not_13 (not_13_out, BCD[0]);
  not not_14 (not_14_out, BCD[0]);
  not not_15 (not_15_out, BCD[2]);
  not not_16 (not_16_out, BCD[0]);
  not not_17 (not_17_out, BCD[2]);
  not not_18 (not_18_out, BCD[0]);
  not not_19 (not_19_out, BCD[1]);
  not not_20 (not_20_out, BCD[1]);
  and and_1 (and_1_out, not_1_out, BCD[1]);
  and and_2 (and_2_out, BCD[1], not_2_out);
  and and_3 (and_3_out, BCD[2], not_3_out);
  and and_4 (and_4_out, not_4_out, not_5_out);
  and and_5 (and_5_out, BCD[2], not_6_out);
  and and_6 (and_6_out, BCD[2], not_7_out);
  and and_7 (and_7_out, not_8_out, not_9_out);
  and and_8 (and_8_out, BCD[2], BCD[0]);
  not not_21 (not_21_out, BCD[2]);
  and and_9 (and_9_out, not_10_out, not_11_out);
  and and_10 (and_10_out, BCD[1], BCD[0]);
  and and_11 (and_11_out, not_12_out, not_13_out);
  and and_12 (and_12_out, BCD[1], not_14_out);
  and and_13 (and_13_out, not_15_out, not_16_out);
  and and_14 (and_14_out, not_17_out, BCD[1]);
  and and_15 (and_15_out, BCD[1], not_18_out);
  and and_16 (and_16_out, BCD[2], not_19_out, BCD[0]);
  or or_1 (out_2[6], not_20_out, BCD[0], BCD[2]);
  or or_2 (out_2[0], and_1_out, and_2_out, and_3_out, BCD[3]);
  or or_3 (out_2[1], and_4_out, and_5_out, and_6_out, BCD[3]);
  or or_4 (out_2[2], and_7_out, BCD[1], and_8_out, BCD[3]);
  or or_5 (out_2[3], not_21_out, and_9_out, and_10_out);
  or or_6 (out_2[4], and_11_out, and_12_out);
  or or_7 (out_2[5], and_13_out, and_14_out, and_15_out, and_16_out);
endmodule

module BinaryToBCD (
  input  [31:0] Input,
  output Minus,
  output [3:0] BCD9,
  output [3:0] BCD8,
  output [3:0] BCD7,
  output [3:0] BCD6,
  output [3:0] BCD5,
  output [3:0] BCD4,
  output [3:0] BCD3,
  output [3:0] BCD2,
  output [3:0] BCD1,
  output [3:0] BCD0
);

  wire [27:0] subtractor_1_out, subtractor_2_out, subtractor_3_out, subtractor_4_out, subtractor_5_out,
       subtractor_6_out, subtractor_7_out, subtractor_8_out, subtractor_9_out;
  wire [31:0] adder_1_out, divider_1_out, divider_2_out, divider_3_out, divider_4_out, divider_5_out,
       divider_6_out, divider_7_out, divider_8_out, multiplexer_1_out, multiplier_1_out, multiplier_2_out,
       multiplier_3_out, multiplier_4_out, multiplier_5_out, multiplier_6_out, multiplier_7_out,
       multiplier_8_out, multiplier_9_out, not_1_out;
  wire [31:4] divider_9_out;

  assign not_1_out = ~Input;  // NOT_Gate not_1, 32 bits wide
  Adder #(.width(32)) adder_1 (.a(not_1_out), .b(32'h1), .out(adder_1_out));  // open: cin, cout
  Multiplexer #(.width(32)) multiplexer_1 (
    .in0(Input), .in1(adder_1_out), .out(multiplexer_1_out), .sel(Input[31]));  // open: en
  Subtractor #(.width(32)) subtractor_1 (
    .a(multiplexer_1_out), .b(multiplier_1_out), .out({subtractor_1_out, BCD0}));  // open: bin, bout
  Multiplier #(.width(32)) multiplier_1 (.a(divider_1_out), .b(32'ha), .out(multiplier_1_out));  // open: cin, cout
  Divider #(.width(32)) divider_1 (.a(multiplexer_1_out), .b(32'ha), .out(divider_1_out));  // open: upper, rem
  Subtractor #(.width(32)) subtractor_2 (
    .a(divider_1_out), .b(multiplier_2_out), .out({subtractor_2_out, BCD1}));  // open: bin, bout
  Multiplier #(.width(32)) multiplier_2 (.a(divider_2_out), .b(32'ha), .out(multiplier_2_out));  // open: cin, cout
  Divider #(.width(32)) divider_2 (.a(divider_1_out), .b(32'ha), .out(divider_2_out));  // open: upper, rem
  Subtractor #(.width(32)) subtractor_3 (
    .a(divider_2_out), .b(multiplier_3_out), .out({subtractor_3_out, BCD2}));  // open: bin, bout
  Multiplier #(.width(32)) multiplier_3 (.a(divider_3_out), .b(32'ha), .out(multiplier_3_out));  // open: cin, cout
  Divider #(.width(32)) divider_3 (.a(divider_2_out), .b(32'ha), .out(divider_3_out));  // open: upper, rem
  Subtractor #(.width(32)) subtractor_4 (
    .a(divider_3_out), .b(multiplier_4_out), .out({subtractor_4_out, BCD3}));  // open: bin, bout
  Multiplier #(.width(32)) multiplier_4 (.a(divider_4_out), .b(32'ha), .out(multiplier_4_out));  // open: cin, cout
  Divider #(.width(32)) divider_4 (.a(divider_3_out), .b(32'ha), .out(divider_4_out));  // open: upper, rem
  Subtractor #(.width(32)) subtractor_5 (
    .a(divider_4_out), .b(multiplier_5_out), .out({subtractor_5_out, BCD4}));  // open: bin, bout
  Multiplier #(.width(32)) multiplier_5 (.a(divider_5_out), .b(32'ha), .out(multiplier_5_out));  // open: cin, cout
  Divider #(.width(32)) divider_5 (.a(divider_4_out), .b(32'ha), .out(divider_5_out));  // open: upper, rem
  Subtractor #(.width(32)) subtractor_6 (
    .a(divider_5_out), .b(multiplier_6_out), .out({subtractor_6_out, BCD5}));  // open: bin, bout
  Multiplier #(.width(32)) multiplier_6 (.a(divider_6_out), .b(32'ha), .out(multiplier_6_out));  // open: cin, cout
  Divider #(.width(32)) divider_6 (.a(divider_5_out), .b(32'ha), .out(divider_6_out));  // open: upper, rem
  Subtractor #(.width(32)) subtractor_7 (
    .a(divider_6_out), .b(multiplier_7_out), .out({subtractor_7_out, BCD6}));  // open: bin, bout
  Multiplier #(.width(32)) multiplier_7 (.a(divider_7_out), .b(32'ha), .out(multiplier_7_out));  // open: cin, cout
  Divider #(.width(32)) divider_7 (.a(divider_6_out), .b(32'ha), .out(divider_7_out));  // open: upper, rem
  Subtractor #(.width(32)) subtractor_8 (
    .a(divider_7_out), .b(multiplier_8_out), .out({subtractor_8_out, BCD7}));  // open: bin, bout
  Multiplier #(.width(32)) multiplier_8 (.a(divider_8_out), .b(32'ha), .out(multiplier_8_out));  // open: cin, cout
  Divider #(.width(32)) divider_8 (.a(divider_7_out), .b(32'ha), .out(divider_8_out));  // open: upper, rem
  Subtractor #(.width(32)) subtractor_9 (
    .a(divider_8_out), .b(multiplier_9_out), .out({subtractor_9_out, BCD8}));  // open: bin, bout
  Multiplier #(.width(32)) multiplier_9 (
    .a({divider_9_out, BCD9}), .b(32'ha), .out(multiplier_9_out));  // open: cin, cout
  Divider #(.width(32)) divider_9 (.a(divider_8_out), .b(32'ha), .out({divider_9_out, BCD9}));  // open: upper, rem

  assign Minus = Input[31];
endmodule

module Keypad_Controller (
  input  C,
  input  in_2,
  input  in_3,
  input  in_4,
  input  in_5,
  input  in_6,
  input  _9,
  input  _8,
  input  _7,
  input  _6,
  input  _5,
  input  _4,
  input  _3,
  input  _2,
  input  _1,
  input  _0,
  input  [31:0] From__t9,
  output Write,
  output [31:0] Output
);

  wire iszero_1_out_2, iszero_2_out_2;
  wire [3:0] or_4_out;
  wire [15:0] and_1_out;

  and and_1 (and_1_out[0], C, iszero_1_out_2);
  and and_2 (and_1_out[1], in_2, iszero_1_out_2);
  and and_3 (and_1_out[2], in_3, iszero_1_out_2);
  and and_4 (and_1_out[3], in_4, iszero_1_out_2);
  and and_5 (and_1_out[4], in_5, iszero_1_out_2);
  and and_6 (and_1_out[5], in_6, iszero_1_out_2);
  and and_7 (and_1_out[6], _9, iszero_1_out_2);
  and and_8 (and_1_out[7], _8, iszero_1_out_2);
  and and_9 (and_1_out[8], _7, iszero_1_out_2);
  and and_10 (and_1_out[9], _6, iszero_1_out_2);
  and and_11 (and_1_out[10], _5, iszero_1_out_2);
  and and_12 (and_1_out[11], _4, iszero_1_out_2);
  and and_13 (and_1_out[12], _3, iszero_1_out_2);
  and and_14 (and_1_out[13], _2, iszero_1_out_2);
  and and_15 (and_1_out[14], _1, iszero_1_out_2);
  and and_16 (and_1_out[15], _0, iszero_1_out_2);
  isZero iszero_1 (.Input(From__t9), .out_2(iszero_1_out_2));
  or or_1 (or_4_out[3], and_1_out[0], and_1_out[1], and_1_out[2], and_1_out[3], and_1_out[4], and_1_out[5], and_1_out[6], and_1_out[7]);
  or or_2 (or_4_out[2], and_1_out[8], and_1_out[9], and_1_out[10], and_1_out[11], and_1_out[0], and_1_out[1], and_1_out[2], and_1_out[3]);
  or or_3 (or_4_out[1], and_1_out[12], and_1_out[13], and_1_out[9], and_1_out[8], and_1_out[5], and_1_out[4], and_1_out[1], and_1_out[0]);
  or or_4 (or_4_out[0], and_1_out[12], and_1_out[14], and_1_out[10], and_1_out[8], and_1_out[6], and_1_out[4], and_1_out[2], and_1_out[0]);
  isZero iszero_2 (.Input({{16{1'b0}}, and_1_out}), .out_2(iszero_2_out_2));
  not not_1 (Write, iszero_2_out_2);
  assign Output = Write ? {28'h8000000, or_4_out} : 32'bz;  // Controlled_Buffer controlled_buffer_1
endmodule

module isZero (
  input  [31:0] Input,
  output out_2
);

  wire or_1_out;

  not not_1 (out_2, or_1_out);
  or or_1 (or_1_out, Input[0], Input[1], Input[2], Input[3], Input[4], Input[5], Input[6], Input[7], Input[8], Input[9], Input[10], Input[11], Input[12], Input[13], Input[14], Input[15], Input[16], Input[17], Input[18], Input[19], Input[20], Input[21], Input[22], Input[23], Input[24], Input[25], Input[26], Input[27], Input[28], Input[29], Input[30], Input[31]);
endmodule

module Instruction_Memory__TO_DO (
  input  [15:0] PC,
  output [31:0] DataOutput
);

  ROM #(.addrWidth(16), .dataWidth(32)) rom_1 (.addr(PC), .data(DataOutput), .sel(1'b1));

  // Notes on the sheet:
  //   contents of rom_1 (hex, n*v repeats v):
  //   2010000a 2011000b 2012000c 2013000d 2014000e 2015000f 20160009 4020 4820 5020 5820 6020 6820 c020
  //   c820 6020 1320ffff 3339000f 13300042 13310041 13320040 1333003f 1334003a 1335ffe8 5820 12c6020
  //   216b0001 1576fffd 1994820 96020 9c020 c820 6820 8100010 1320ffff 3339000f 13300030 1331002f 1332002e
  //   1333002d 13340028 1335ffd6 5820 a6020 14c6020 216b0001 1576fffd 1995020 a6020 ac020 c820 1320ffff
  //   3339000f 13300023 13310022 13320021 13330020 13340023 1335ffc5 5820 a6020 14c6020 216b0001 1576fffd
  //   1995020 a6020 ac020 c820 8100033 1320ffff 3339000f 1330000d 1331000c 1332000b 1333000a 13340005
  //   1335ffb3 194820 9c020 c820 810000f 96820 dc020 c820 8100045 1540ffdd 194020 c820 8100022 11100007
  //   11110014 11120021 1113003a 1110000a 11110017 1112002a 11130045 12a6820 dc020 d4820 194020 5020 c820
  //   8100022 12a6820 dc020 d4820 4020 5020 c820 8100045 12a6822 dc020 d4820 194020 5020 c820 8100022
  //   12a6822 dc020 d4820 4020 5020 c820 8100045 6820 5820 11200035 11400034 1a96820 216b0001 156afffd
  //   dc020 d4820 194020 5020 c820 8100022 6820 5820 1120002f 1140002e 1a96820 216b0001 156afffd dc020
  //   d4820 4020 5020 c820 8100045 6820 120582a 15600029 5820 11200019 12a4822 21ad0001 12a582a 1160fffc
  //   dc020 d4820 194020 5020 c820 8100022 6820 120582a 15600029 5820 1120000a 12a4822 21ad0001 12a582a
  //   1160fffc dc020 d4820 4020 5020 c820 8100045 194020 4820 5020 6820 c020 c820 8100022 4020 4820 5020
  //   6820 c020 c820 8100045 5820 1204827 21290001 12a4822 21ad0001 12a582a 1560fffc 1a06827 21ad0001
  //   dc020 d4820 194020 5020 c820 8100022 5820 1204827 21290001 12a4822 21ad0001 12a582a 1160fffc 1a06827
  //   21ad0001 dc020 d4820 4020 5020 c820 8100045
endmodule

module Shift_Left__TO_DO (
  input  [31:0] Input,
  input  [4:0] Shamt,
  output [31:0] Output
);

  wire [31:0] decoder_1_out0;

  Decoder #(.select(5), .enable("false")) decoder_1 (
    .out0(decoder_1_out0[0]), .out1(decoder_1_out0[1]), .out2(decoder_1_out0[2]), .out3(decoder_1_out0[3]),
    .out4(decoder_1_out0[4]), .out5(decoder_1_out0[5]), .out6(decoder_1_out0[6]), .out7(decoder_1_out0[7]),
    .out8(decoder_1_out0[8]), .out9(decoder_1_out0[9]), .out10(decoder_1_out0[10]),
    .out11(decoder_1_out0[11]), .out12(decoder_1_out0[12]), .out13(decoder_1_out0[13]),
    .out14(decoder_1_out0[14]), .out15(decoder_1_out0[15]), .out16(decoder_1_out0[16]),
    .out17(decoder_1_out0[17]), .out18(decoder_1_out0[18]), .out19(decoder_1_out0[19]),
    .out20(decoder_1_out0[20]), .out21(decoder_1_out0[21]), .out22(decoder_1_out0[22]),
    .out23(decoder_1_out0[23]), .out24(decoder_1_out0[24]), .out25(decoder_1_out0[25]),
    .out26(decoder_1_out0[26]), .out27(decoder_1_out0[27]), .out28(decoder_1_out0[28]),
    .out29(decoder_1_out0[29]), .out30(decoder_1_out0[30]), .out31(decoder_1_out0[31]), .sel(Shamt));
  Multiplier #(.width(32)) multiplier_1 (.a(Input), .b(decoder_1_out0), .out(Output));  // open: cin, cout
endmodule

module Shift_Right__TO_DO (
  input  [31:0] Input,
  input  [4:0] Shamt,
  output [31:0] Output
);

  wire [31:0] decoder_1_out0;

  Decoder #(.select(5), .enable("false")) decoder_1 (
    .out0(decoder_1_out0[0]), .out1(decoder_1_out0[1]), .out2(decoder_1_out0[2]), .out3(decoder_1_out0[3]),
    .out4(decoder_1_out0[4]), .out5(decoder_1_out0[5]), .out6(decoder_1_out0[6]), .out7(decoder_1_out0[7]),
    .out8(decoder_1_out0[8]), .out9(decoder_1_out0[9]), .out10(decoder_1_out0[10]),
    .out11(decoder_1_out0[11]), .out12(decoder_1_out0[12]), .out13(decoder_1_out0[13]),
    .out14(decoder_1_out0[14]), .out15(decoder_1_out0[15]), .out16(decoder_1_out0[16]),
    .out17(decoder_1_out0[17]), .out18(decoder_1_out0[18]), .out19(decoder_1_out0[19]),
    .out20(decoder_1_out0[20]), .out21(decoder_1_out0[21]), .out22(decoder_1_out0[22]),
    .out23(decoder_1_out0[23]), .out24(decoder_1_out0[24]), .out25(decoder_1_out0[25]),
    .out26(decoder_1_out0[26]), .out27(decoder_1_out0[27]), .out28(decoder_1_out0[28]),
    .out29(decoder_1_out0[29]), .out30(decoder_1_out0[30]), .out31(decoder_1_out0[31]), .sel(Shamt));
  Divider #(.width(32)) divider_1 (.a(Input), .b(decoder_1_out0), .out(Output));  // open: upper, rem
endmodule

module Sign_Extend__TO_DO (
  input  [15:0] Input,
  output [31:0] out_2
);


  assign out_2 = {{17{Input[15]}}, Input[14:0]};
endmodule

module _32_bit_ALU__TO_DO (
  input  [31:0] A,
  input  [31:0] B,
  input  [4:0] Shamt,
  input  [5:0] Control,
  output Zero,
  output [31:0] Result
);

  wire [31:0] adder_1_out, and_1_out, multiplexer_1_out, multiplexer_2_out, multiplexer_3_out, not_1_out,
       not_2_out, or_1_out, sll_output, srl_output;

  assign not_1_out = ~A;  // NOT_Gate not_1, 32 bits wide
  Multiplexer #(.width(32), .enable("false")) multiplexer_1 (
    .in0(A), .in1(not_1_out), .out(multiplexer_1_out), .sel(Control[5]));
  Multiplexer #(.width(32), .enable("false")) multiplexer_2 (
    .in0(B), .in1(not_2_out), .out(multiplexer_2_out), .sel(Control[4]));
  assign not_2_out = ~B;  // NOT_Gate not_2, 32 bits wide
  Shift_Left__TO_DO sll (.Input(B), .Shamt(Shamt), .Output(sll_output));
  Shift_Right__TO_DO srl (.Input(B), .Shamt(Shamt), .Output(srl_output));
  assign and_1_out = multiplexer_1_out & multiplexer_2_out;  // AND_Gate and_1, 32 bits wide
  assign or_1_out = multiplexer_1_out | multiplexer_2_out;  // OR_Gate or_1, 32 bits wide
  Adder #(.width(32)) adder_1 (
    .a(multiplexer_1_out), .b(multiplexer_2_out), .out(adder_1_out), .cin(Control[4]));  // open: cout
  Multiplexer #(.select(2), .width(32), .enable("false")) multiplexer_3 (
    .in0(and_1_out), .in1(or_1_out), .in2(adder_1_out), .in3({{31{1'b0}}, adder_1_out[31]}),
    .out(multiplexer_3_out), .sel(Control[3:2]));
  isZero iszero_1 (.Input(multiplexer_3_out), .out_2(Zero));
  Multiplexer #(.select(2), .width(32), .enable("false")) multiplexer_4 (
    .in0(multiplexer_3_out), .in2(sll_output), .in3(srl_output), .out(Result), .sel(Control[1:0]));  // open: in1
endmodule

module Register_File__TO_DO (
  input  [4:0] ReadReg1,
  input  [4:0] ReadReg2,
  input  RegWrite,
  input  [4:0] WriteRegister,
  input  [31:0] WriteData,
  input  Clock,
  input  [31:0] Write_t9Keypad,
  input  WriteSignalKeypad,
  output [31:0] ReadData1,
  output [31:0] ReadData2,
  output [31:0] t8_to_LCD,
  output [31:0] t9_to_Keypad
);

  wire and_1_out, and_2_out, and_3_out, and_4_out, and_5_out, and_6_out, and_7_out, and_8_out, and_9_out,
       and_10_out, and_11_out, and_12_out, and_13_out, and_14_out, and_15_out, and_16_out, and_17_out,
       and_18_out, and_19_out, and_20_out, and_21_out, and_22_out, and_23_out, and_24_out, and_25_out,
       and_26_out, and_27_out, and_28_out, and_29_out, and_30_out, and_31_out, and_32_out,
       controlled_buffer_2_out, decoder_1_out0, decoder_1_out1, decoder_1_out2, decoder_1_out3,
       decoder_1_out4, decoder_1_out5, decoder_1_out6, decoder_1_out7, decoder_1_out8, decoder_1_out9,
       decoder_1_out10, decoder_1_out11, decoder_1_out12, decoder_1_out13, decoder_1_out14, decoder_1_out15,
       decoder_1_out16, decoder_1_out17, decoder_1_out18, decoder_1_out19, decoder_1_out20, decoder_1_out21,
       decoder_1_out22, decoder_1_out23, decoder_1_out24, decoder_1_out25, decoder_1_out26, decoder_1_out27,
       decoder_1_out28, decoder_1_out29, decoder_1_out30, decoder_1_out31;
  wire [31:0] controlled_buffer_1_out, Register_0_q, Register_1_q, Register_2_q, Register_3_q, Register_4_q,
       Register_6_q, Register_7_q, Register_8_q, Register_9_q, Register_10_q, Register_11_q, Register_12_q,
       Register_13_q, Register_14_q, Register_15_q, Register_16_q, Register_17_q, Register_18_q,
       Register_19_q, Register_20_q, Register_21_q, Register_22_q, Register_23_q, Register_26_q,
       Register_27_q, Register_28_q, Register_29_q, Register_30_q, Register_31_q, undriven;

  Decoder #(.select(5), .enable("false")) decoder_1 (
    .out0(decoder_1_out0), .out1(decoder_1_out1), .out2(decoder_1_out2), .out3(decoder_1_out3),
    .out4(decoder_1_out4), .out5(decoder_1_out5), .out6(decoder_1_out6), .out7(decoder_1_out7),
    .out8(decoder_1_out8), .out9(decoder_1_out9), .out10(decoder_1_out10), .out11(decoder_1_out11),
    .out12(decoder_1_out12), .out13(decoder_1_out13), .out14(decoder_1_out14), .out15(decoder_1_out15),
    .out16(decoder_1_out16), .out17(decoder_1_out17), .out18(decoder_1_out18), .out19(decoder_1_out19),
    .out20(decoder_1_out20), .out21(decoder_1_out21), .out22(decoder_1_out22), .out23(decoder_1_out23),
    .out24(decoder_1_out24), .out25(decoder_1_out25), .out26(decoder_1_out26), .out27(decoder_1_out27),
    .out28(decoder_1_out28), .out29(decoder_1_out29), .out30(decoder_1_out30), .out31(decoder_1_out31),
    .sel(WriteRegister));
  assign controlled_buffer_1_out = WriteSignalKeypad ? Write_t9Keypad : 32'bz;  // Controlled_Buffer controlled_buffer_1
  assign controlled_buffer_2_out = WriteSignalKeypad ? WriteSignalKeypad : 1'bz;  // Controlled_Buffer controlled_buffer_2
  assign controlled_buffer_1_out = and_1_out ? WriteData : 32'bz;  // Controlled_Buffer controlled_buffer_3
  assign controlled_buffer_2_out = and_1_out ? and_1_out : 1'bz;  // Controlled_Buffer controlled_buffer_4
  and and_1 (and_1_out, RegWrite, decoder_1_out25);
  and and_2 (and_2_out, RegWrite, decoder_1_out0);
  and and_3 (and_3_out, RegWrite, decoder_1_out1);
  and and_4 (and_4_out, RegWrite, decoder_1_out2);
  and and_5 (and_5_out, RegWrite, decoder_1_out3);
  and and_6 (and_6_out, RegWrite, decoder_1_out4);
  and and_7 (and_7_out, RegWrite, decoder_1_out5);
  and and_8 (and_8_out, RegWrite, decoder_1_out6);
  and and_9 (and_9_out, RegWrite, decoder_1_out7);
  and and_10 (and_10_out, RegWrite, decoder_1_out8);
  and and_11 (and_11_out, RegWrite, decoder_1_out9);
  and and_12 (and_12_out, RegWrite, decoder_1_out10);
  and and_13 (and_13_out, RegWrite, decoder_1_out11);
  and and_14 (and_14_out, RegWrite, decoder_1_out12);
  and and_15 (and_15_out, RegWrite, decoder_1_out13);
  and and_16 (and_16_out, RegWrite, decoder_1_out14);
  and and_17 (and_17_out, RegWrite, decoder_1_out15);
  and and_18 (and_18_out, RegWrite, decoder_1_out16);
  and and_19 (and_19_out, RegWrite, decoder_1_out17);
  and and_20 (and_20_out, RegWrite, decoder_1_out18);
  and and_21 (and_21_out, RegWrite, decoder_1_out19);
  and and_22 (and_22_out, RegWrite, decoder_1_out20);
  and and_23 (and_23_out, RegWrite, decoder_1_out21);
  and and_24 (and_24_out, RegWrite, decoder_1_out22);
  and and_25 (and_25_out, RegWrite, decoder_1_out23);
  and and_26 (and_26_out, RegWrite, decoder_1_out24);
  and and_27 (and_27_out, RegWrite, decoder_1_out26);
  and and_28 (and_28_out, RegWrite, decoder_1_out27);
  and and_29 (and_29_out, RegWrite, decoder_1_out28);
  and and_30 (and_30_out, RegWrite, decoder_1_out29);
  and and_31 (and_31_out, RegWrite, decoder_1_out30);
  and and_32 (and_32_out, RegWrite, decoder_1_out31);
  Register #(.width(32)) Register_0 (.D(WriteData), .en(and_2_out), .Q(Register_0_q), .clk(Clock));  // open: clr
  Register #(.width(32)) Register_1 (.D(WriteData), .en(and_3_out), .Q(Register_1_q), .clk(Clock));  // open: clr
  Register #(.width(32)) Register_2 (.D(WriteData), .en(and_4_out), .Q(Register_2_q), .clk(Clock));  // open: clr
  Register #(.width(32)) Register_3 (.D(WriteData), .en(and_5_out), .Q(Register_3_q), .clk(Clock));  // open: clr
  Register #(.width(32)) Register_4 (.D(WriteData), .en(and_6_out), .Q(Register_4_q), .clk(Clock));  // open: clr
  Register #(.width(32)) Register_5 (.D(WriteData), .en(and_7_out), .clk(Clock));  // open: Q, clr
  Register #(.width(32)) Register_6 (.D(WriteData), .en(and_8_out), .Q(Register_6_q), .clk(Clock));  // open: clr
  Register #(.width(32)) Register_7 (.D(WriteData), .en(and_9_out), .Q(Register_7_q), .clk(Clock));  // open: clr
  Register #(.width(32)) Register_8 (.D(WriteData), .en(and_10_out), .Q(Register_8_q), .clk(Clock));  // open: clr
  Register #(.width(32)) Register_9 (.D(WriteData), .en(and_11_out), .Q(Register_9_q), .clk(Clock));  // open: clr
  Register #(.width(32)) Register_10 (.D(WriteData), .en(and_12_out), .Q(Register_10_q), .clk(Clock));  // open: clr
  Register #(.width(32)) Register_11 (.D(WriteData), .en(and_13_out), .Q(Register_11_q), .clk(Clock));  // open: clr
  Register #(.width(32)) Register_12 (.D(WriteData), .en(and_14_out), .Q(Register_12_q), .clk(Clock));  // open: clr
  Register #(.width(32)) Register_13 (.D(WriteData), .en(and_15_out), .Q(Register_13_q), .clk(Clock));  // open: clr
  Register #(.width(32)) Register_14 (.D(WriteData), .en(and_16_out), .Q(Register_14_q), .clk(Clock));  // open: clr
  Register #(.width(32)) Register_15 (.D(WriteData), .en(and_17_out), .Q(Register_15_q), .clk(Clock));  // open: clr
  Register #(.width(32)) Register_16 (.D(WriteData), .en(and_18_out), .Q(Register_16_q), .clk(Clock));  // open: clr
  Register #(.width(32)) Register_17 (.D(WriteData), .en(and_19_out), .Q(Register_17_q), .clk(Clock));  // open: clr
  Register #(.width(32)) Register_18 (.D(WriteData), .en(and_20_out), .Q(Register_18_q), .clk(Clock));  // open: clr
  Register #(.width(32)) Register_19 (.D(WriteData), .en(and_21_out), .Q(Register_19_q), .clk(Clock));  // open: clr
  Register #(.width(32)) Register_20 (.D(WriteData), .en(and_22_out), .Q(Register_20_q), .clk(Clock));  // open: clr
  Register #(.width(32)) Register_21 (.D(WriteData), .en(and_23_out), .Q(Register_21_q), .clk(Clock));  // open: clr
  Register #(.width(32)) Register_22 (.D(WriteData), .en(and_24_out), .Q(Register_22_q), .clk(Clock));  // open: clr
  Register #(.width(32)) Register_23 (.D(WriteData), .en(and_25_out), .Q(Register_23_q), .clk(Clock));  // open: clr
  Register #(.width(32)) t8 (.D(WriteData), .en(and_26_out), .Q(t8_to_LCD), .clk(Clock));  // open: clr
  Register #(.width(32)) t9 (
    .D(controlled_buffer_1_out), .en(controlled_buffer_2_out), .Q(t9_to_Keypad), .clk(Clock));  // open: clr
  Register #(.width(32)) Register_26 (.D(WriteData), .en(and_27_out), .Q(Register_26_q), .clk(Clock));  // open: clr
  Register #(.width(32)) Register_27 (.D(WriteData), .en(and_28_out), .Q(Register_27_q), .clk(Clock));  // open: clr
  Register #(.width(32)) Register_28 (.D(WriteData), .en(and_29_out), .Q(Register_28_q), .clk(Clock));  // open: clr
  Register #(.width(32)) Register_29 (.D(WriteData), .en(and_30_out), .Q(Register_29_q), .clk(Clock));  // open: clr
  Register #(.width(32)) Register_30 (.D(WriteData), .en(and_31_out), .Q(Register_30_q), .clk(Clock));  // open: clr
  Register #(.width(32)) Register_31 (.D(WriteData), .en(and_32_out), .Q(Register_31_q), .clk(Clock));  // open: clr
  Multiplexer #(.select(5), .width(32), .enable("false")) multiplexer_1 (
    .in0(Register_0_q), .in1(Register_1_q), .in2(Register_2_q), .in3(Register_3_q), .in4(Register_4_q),
    .in5(undriven), .in6(Register_6_q), .in7(Register_7_q), .in8(Register_8_q), .in9(Register_9_q),
    .in10(Register_10_q), .in11(Register_11_q), .in12(Register_12_q), .in13(Register_13_q),
    .in14(Register_14_q), .in15(Register_15_q), .in16(Register_16_q), .in17(Register_17_q),
    .in18(Register_18_q), .in19(Register_19_q), .in20(Register_20_q), .in21(Register_21_q),
    .in22(Register_22_q), .in23(Register_23_q), .in24(t8_to_LCD), .in25(t9_to_Keypad), .in26(Register_26_q),
    .in27(Register_27_q), .in28(Register_28_q), .in29(Register_29_q), .in30(Register_30_q),
    .in31(Register_31_q), .out(ReadData1), .sel(ReadReg1));
  Multiplexer #(.select(5), .width(32), .enable("false")) multiplexer_2 (
    .in0(Register_0_q), .in1(Register_1_q), .in2(Register_2_q), .in3(Register_3_q), .in4(Register_4_q),
    .in5(undriven), .in6(Register_6_q), .in7(Register_7_q), .in8(Register_8_q), .in9(Register_9_q),
    .in10(Register_10_q), .in11(Register_11_q), .in12(Register_12_q), .in13(Register_13_q),
    .in14(Register_14_q), .in15(Register_15_q), .in16(Register_16_q), .in17(Register_17_q),
    .in18(Register_18_q), .in19(Register_19_q), .in20(Register_20_q), .in21(Register_21_q),
    .in22(Register_22_q), .in23(Register_23_q), .in24(t8_to_LCD), .in25(t9_to_Keypad), .in26(Register_26_q),
    .in27(Register_27_q), .in28(Register_28_q), .in29(Register_29_q), .in30(Register_30_q),
    .in31(Register_31_q), .out(ReadData2), .sel(ReadReg2));
endmodule

module Control_Unit__TO_DO (
  input  [5:0] OPcode,
  output RegDST,
  output Jump,
  output bne,
  output beq,
  output [3:0] ALUop,
  output ALUsrc,
  output RegWrite
);

  wire and_1_out, and_2_out, and_4_out, and_5_out, and_6_out, and_7_out, and_8_out, and_9_out, not_1_out,
       not_2_out, not_3_out, not_4_out, not_5_out, not_6_out;

  not not_1 (not_1_out, OPcode[5]);
  not not_2 (not_2_out, OPcode[3]);
  not not_3 (not_3_out, OPcode[4]);
  not not_4 (not_4_out, OPcode[2]);
  not not_5 (not_5_out, OPcode[1]);
  not not_6 (not_6_out, OPcode[0]);
  and and_1 (and_1_out, not_1_out, not_3_out, not_2_out, not_4_out, not_6_out);
  and and_2 (and_2_out, not_1_out, not_3_out, not_2_out, OPcode[2], not_5_out);
  and and_3 (Jump, not_1_out, not_3_out, not_2_out, not_4_out, OPcode[1], not_6_out);
  and and_4 (and_4_out, not_1_out, not_3_out, not_2_out, OPcode[2], not_5_out);
  and and_5 (and_5_out, not_1_out, not_3_out, OPcode[3], not_4_out, not_6_out);
  and and_6 (and_6_out, not_1_out, not_3_out, OPcode[3], OPcode[2], not_5_out);
  and and_7 (and_7_out, not_1_out, not_3_out, not_4_out, not_5_out, not_6_out);
  and and_8 (and_8_out, not_1_out, not_3_out, OPcode[3], not_4_out, not_6_out);
  and and_9 (and_9_out, not_1_out, not_3_out, OPcode[3], OPcode[2], not_5_out);
  or or_1 (RegDST, and_1_out, and_2_out);
  or or_2 (ALUsrc, and_5_out, and_6_out);
  or or_3 (RegWrite, and_7_out, and_8_out, and_9_out);
  and and_10 (bne, and_4_out, OPcode[0]);
  and and_11 (beq, and_4_out, not_6_out);

  assign ALUop = OPcode[3:0];
endmodule

module PC (
  input  [31:0] PCInput,
  input  Clock,
  output [15:0] PCoutput_prime
);

  wire [31:0] PC_q;

  Register #(.width(32)) PC (
    .D(PCInput), .en(1'b1), .Q({PC_q[31:18], PCoutput_prime, PC_q[1:0]}), .clk(Clock));  // open: clr
endmodule

module ALUcontrol (
  input  [3:0] OP,
  input  [5:0] funct,
  output [5:0] ControlOutput
);

  wire [5:0] functcontrol_output;

  functcontrol functcontrol (.Input(funct), .\output (functcontrol_output));
  Multiplexer #(.select(4), .width(6), .enable("false")) multiplexer_1 (
    .in0(functcontrol_output), .in2({6{1'b0}}), .in4(6'b011000), .in5(6'b011000), .in8(6'b001000),
    .in10(6'b011100), .in12({6{1'b0}}), .in13(6'b000100), .out(ControlOutput), .sel(OP));  // open: in1, in3, in6, in7, in9, in11, in14, in15
endmodule

module ShiftLeft2 (
  input  [25:0] Input,
  output [27:0] JumpAddress
);


  assign JumpAddress = {Input, 2'b00};
endmodule

module PCadd4 (
  input  [15:0] PCinput,
  output [31:0] Output
);

  Adder #(.width(32)) adder_1 (.a(32'h4), .b({{14{1'b0}}, PCinput, 2'b00}), .out(Output));  // open: cin, cout
endmodule

module functcontrol (
  input  [5:0] Input,
  output [5:0] \output 
);

  wire and_1_out, and_2_out, and_3_out, and_4_out, and_5_out, and_6_out, not_1_out, not_2_out, not_3_out,
       not_5_out;

  not not_1 (not_1_out, Input[3]);
  not not_2 (not_2_out, Input[1]);
  not not_3 (not_3_out, Input[2]);
  not not_4 (\output [1], Input[5]);
  not not_5 (not_5_out, Input[0]);
  and and_1 (and_1_out, not_1_out, Input[2], not_2_out, Input[0]);
  and and_2 (and_2_out, Input[3], not_3_out, Input[1], not_5_out);
  and and_3 (and_3_out, not_1_out, not_3_out, not_5_out);
  and and_4 (and_4_out, not_3_out, Input[1], not_5_out);
  and and_5 (and_5_out, not_3_out, Input[1], not_5_out);
  and and_6 (and_6_out, not_1_out, Input[2], Input[1], Input[0]);
  and and_7 (\output [5], not_1_out, Input[2], Input[1], Input[0]);
  and and_8 (\output [0], \output [1], Input[1]);
  or or_1 (\output [2], and_1_out, and_2_out);
  or or_2 (\output [3], and_3_out, and_4_out);
  or or_3 (\output [4], and_5_out, and_6_out);
endmodule
